# Fritzing sketch arduino_lightup_skull_schematics (saved by Fritzing 0.9.3b)
breadboards: 1

parts:
  Part1 = Arduino Nano (Rev3.0)
  hc-sr3 = hc-sr04
  R1 = Resistor [tolerance=±5% resistance=100 package=THT]
  R2 = Resistor [tolerance=±5% resistance=100 package=THT]
  R3 = Resistor [tolerance=±5% resistance=100 package=THT]
  R4 = Resistor [tolerance=±5% resistance=100 package=THT]
  LED1 = LED - 5mm [color="Red (633nm)" package="5 mm [THT]"]
  LED2 = LED - 5mm [color="Red (633nm)" package="5 mm [THT]"]

nets:
  N1: Part1.GND, R1.Pin_1, LED1.cathode, LED2.cathode
  N2: Part1.D7, LED2.anode
  N3: Part1.D8, LED1.anode
  N4: Part1.D10, R4.Pin_1
  N5: Part1.D11/MOSI, R3.Pin_1
  N6: Part1.5V, R2.Pin_1
  N7: hc-sr3.VCC, R2.Pin_0
  N8: hc-sr3.Trig, R3.Pin_0
  N9: hc-sr3.Echo, R4.Pin_0
  N10: hc-sr3.GND, R1.Pin_0
